# Fritzing sketch wiring (saved by Fritzing 0.9.0b)

parts:
  Arduino = Arduino Pro Mini v13
  C1 = Electrolytic Capacitor [capacitance=4.7µF package="100 mil [THT, electrolytic]"]
  Radio_Module = NRF24L01

nets:
  GND: Arduino.GND, C1.-, Radio_Module.GND
  VCC: Arduino.VCC, C1.+, Radio_Module.VCC
  N1: Arduino.D13/SCK, Radio_Module.SCK
  N2: Arduino.D12/MISO, Radio_Module.MISO
  N3: Arduino.D11_PWM/MOSI, Radio_Module.MOSI
  N4: Arduino.D10_PWM/SS, Radio_Module.CSN
  N5: Arduino.D9_PWM, Radio_Module.CE
  N6: Arduino.D2, Radio_Module.IRQ

custom parts:
  NRF24L01: NRF24L01 module
